# Fritzing sketch Bluetooth (saved by Fritzing 0.9.3b)
circuit board: 8.46667cm x 5.64444cm
breadboards: 1

parts:
  Part1 = Bluetooth HC-05 Macho  # not connected
  J1 = female pin header, 9 pins [form="♀ (female)"]
  Part2 = Arduino Uno (Rev3)

nets:
  N1: J1.pin1, Part2.GND
  N2: J1.pin2, Part2.5V
  N3: J1.pin3, Part2.D4
  N4: J1.pin4, Part2.D5_PWM
  N5: J1.pin5, Part2.D6_PWM
  N6: J1.pin7, Part2.D11_PWM/MOSI
  N7: J1.pin8, Part2.D12/MISO
  N8: J1.pin9, Part2.D13/SCK
